# Fritzing sketch schema (saved by Fritzing 0.7.11b)
breadboards: 1

parts:
  Arduino_Ethernet_Shield = Arduino Ethernet Shield
  Arduino_Mega_2560 = Arduino Mega
  RFM12b1 = RFM12b HopeRF Transceiver
  RTC1 = DS1307 RTC Breakout
  R1 = Resistor [tolerance=±5% resistance=4.7k package=THT]
  R2 = Resistor [tolerance=±5% resistance=10k package=THT]
  R3 = Resistor [tolerance=±5% resistance=10k package=THT]
  R4 = Resistor [tolerance=±5% resistance=4.7k package=THT]
  R5 = Resistor [tolerance=±5% resistance=10k package=THT]
  R6 = Resistor [tolerance=±5% resistance=4.7k package=THT]

nets:
  N1: Arduino_Ethernet_Shield.D2, RFM12b1.6_nRES
  N2: Arduino_Ethernet_Shield.3V3, RFM12b1.9_VDD
  +5V: Arduino_Ethernet_Shield.+5V, RTC1.5V
  N3: Arduino_Ethernet_Shield.GND#19, RTC1.GND
  N4: Arduino_Ethernet_Shield.GND#20, R2.Pin_1, R3.Pin_0, R5.Pin_1
  N5: Arduino_Mega_2560.D20, RTC1.SDA
  N6: Arduino_Mega_2560.D21, RTC1.SCL
  N7: Arduino_Mega_2560.D50, RFM12b1.1_SDO
  N8: Arduino_Mega_2560.D51, R1.Pin_1, R2.Pin_0
  N9: Arduino_Mega_2560.D52, R4.Pin_1, R5.Pin_0
  N10: Arduino_Mega_2560.D53, R6.Pin_1
  N11: RFM12b1.12_SDI, R1.Pin_0
  N12: RFM12b1.13_SCK, R4.Pin_0
  N13: RFM12b1.14_nSEL, R3.Pin_1, R6.Pin_0

custom parts:
  DS1307 RTC Breakout: DS1307 Real-time Clock Breakout Board with Battery
