# Fritzing sketch schema (saved by Fritzing 0.7.11b)
breadboards: 1

parts:
  Part1 = JeeNode wireless microcontroller
  R1 = Resistor [tolerance=±5% resistance=220 package=THT]
  DS1 = DS18B20 1-Wire Temperature Sensor [part_number=DS18B20]
  Q1 = NPN-Transistor [package="TO92 [THT]"]
  R2 = Resistor [tolerance=±5% resistance=220 package=THT]
  LED1 = Blue LED - 5mm
  R3 = Resistor [tolerance=±5% resistance=4.7k package=THT]
  VCC1 = Battery

nets:
  N1: Part1.PWR, DS1.VDD, LED1.anode, R3.Pin_0, VCC1.+
  GND: Part1.GND, DS1.GND, Q1.E, VCC1.-
  N2: Part1.DIO1, DS1.DQ, R3.Pin_1
  N3: Part1.INT2, R2.Pin_0
  N4: R1.Pin_0, LED1.cathode
  N5: R1.Pin_1, Q1.C
  N6: Q1.B, R2.Pin_1

notes:
  Digital temperature meter
  IR LED
